# Fritzing sketch CYTHS (saved by Fritzing 0.9.2b)
circuit board: 1.85361cm x 3.54639cm
breadboards: 1

parts:
  AT85 = attiny85 [package=dip]
  A_R = female pin header, 2 pins [form="♀ (female)"]
  -_+ = female pin header, 2 pins [form="♀ (female)"]
  4_3 = female pin header, 2 pins [form="♀ (female)"]
  A_D_-_+ = female pin header, 2 pins [form="♀ (female)"]
  T433 = female pin header, 2 pins [form="♀ (female)"]
  DHT = Humidity and Temperature Sensor RHT03
  -_- = female pin header, 2 pins [form="♀ (female)"]

nets:
  N1: AT85.Pin_1, A_R.pin1
  N2: AT85.Pin_2, 4_3.pin2
  N3: AT85.Pin_3, 4_3.pin1
  N4: AT85.Pin_4, -_+.pin2, A_D_-_+.pin2, DHT.GND_2, -_-.pin1, -_-.pin2
  N5: AT85.Pin_5, A_D_-_+.pin1, DHT.Vcc
  N6: AT85.Pin_6, T433.pin1
  N7: AT85.Pin_7, DHT.Data-signal
  N8: AT85.Pin_8, -_+.pin1
  N9: A_R.pin2, T433.pin2

notes:
  CYTHS
  v 1.0
